// Logisim project boothie seq.circ as structural Verilog: 1 circuit, main circuit main
module main (
  input  [3:0] AC,
  input  Q_1,
  input  [3:0] Q,
  input  [3:0] M,
  input  in_5,
  input  [3:0] in_6,
  input  [3:0] in_7,
  input  [3:0] in_8,
  input  [3:0] in_9,
  output [1:0] debug,
  output [3:0] AC_2,
  output [3:0] out_12,
  output [8:0] out_13,
  output [8:0] out_14,
  output [3:0] out_15,
  output Qn___1,
  output [3:0] out_17,
  output [1:0] debug_2,
  output [3:0] AC_3,
  output [8:0] out_20,
  output [8:0] out_21,
  output [3:0] out_22,
  output Qn___1_2,
  output [3:0] Q_2,
  output [1:0] debug_3,
  output [3:0] AC_4,
  output [8:0] out_27,
  output [8:0] out_28,
  output [3:0] out_29,
  output Qn___1_3,
  output [3:0] out_31,
  output [1:0] debug_4,
  output [3:0] AC_5,
  output [8:0] out_34,
  output [8:0] out_35,
  output [3:0] out_36,
  output Qn___1_4,
  output [3:0] out_38,
  output [7:0] out_39
);

  wire [3:0] adder_1_out, adder_2_out, adder_3_out, adder_4_out, adder_5_out, adder_6_out, adder_7_out,
       adder_8_out, negator_1_out, negator_2_out, negator_3_out, negator_4_out;

  Negator #(.width(4)) negator_1 (.in(M), .out(negator_1_out));
  Negator #(.width(4)) negator_2 (.in(M), .out(negator_2_out));
  Adder #(.width(4)) adder_1 (.a(M), .b(AC), .out(adder_1_out));  // open: cin, cout
  Negator #(.width(4)) negator_3 (.in(M), .out(negator_3_out));
  Adder #(.width(4)) adder_2 (.a(M), .b(out_14[8:5]), .out(adder_2_out));  // open: cin, cout
  Adder #(.width(4)) adder_3 (.a(out_21[8:5]), .b(M), .out(adder_3_out));  // open: cin, cout
  Negator #(.width(4)) negator_4 (.in(M), .out(negator_4_out));
  Adder #(.width(4)) adder_4 (.a(M), .b(out_28[8:5]), .out(adder_4_out));  // open: cin, cout
  Adder #(.width(4)) adder_5 (.a(AC), .b(negator_2_out), .out(adder_5_out));  // open: cin, cout
  Shifter #(.width(9), .shift("ar")) shifter_1 (.in({AC_2, Q, in_5}), .\dist (in_6), .out({out_14[8:2], debug_2}));
  Shifter #(.width(9), .shift("ar")) shifter_2 (
    .in({AC_3, out_14[4:2], debug_2}), .\dist (in_7), .out({out_21[8:2], debug_3}));
  Shifter #(.width(9), .shift("ar")) shifter_3 (
    .in({AC_4, out_21[4:2], debug_3}), .\dist (in_8), .out({out_28[8:2], debug_4}));
  Adder #(.width(4)) adder_6 (.a(out_28[8:5]), .b(negator_4_out), .out(adder_6_out));  // open: cin, cout
  Shifter #(.width(9), .shift("ar")) shifter_4 (.in({AC_5, out_28[4:2], debug_4}), .\dist (in_9), .out(out_35));
  Adder #(.width(4)) adder_7 (.a(out_14[8:5]), .b(negator_3_out), .out(adder_7_out));  // open: cin, cout
  Adder #(.width(4)) adder_8 (.a(out_21[8:5]), .b(negator_1_out), .out(adder_8_out));  // open: cin, cout
  Multiplexer #(.select(2), .width(4)) multiplexer_1 (
    .in0(AC), .in1(adder_1_out), .in2(adder_5_out), .in3(AC), .out(AC_2), .sel({Q[0], in_5}));  // open: en
  Multiplexer #(.select(2), .width(4)) multiplexer_2 (
    .in0(out_21[8:5]), .in1(adder_3_out), .in2(adder_8_out), .in3(out_21[8:5]), .out(AC_4), .sel(debug_3));  // open: en
  Multiplexer #(.select(2), .width(4)) multiplexer_3 (
    .in0(out_28[8:5]), .in1(adder_4_out), .in2(adder_6_out), .in3(out_28[8:5]), .out(AC_5), .sel(debug_4));  // open: en
  Multiplexer #(.select(2), .width(4), .enable("false")) multiplexer_4 (
    .in0(out_14[8:5]), .in1(adder_2_out), .in2(adder_7_out), .in3(out_14[8:5]), .out(AC_3), .sel(debug_2));

  assign debug = {Q[0], in_5};
  assign out_12 = Q;
  assign out_13 = {AC_2, Q, in_5};
  assign out_14[1:0] = debug_2;
  assign out_15 = out_14[8:5];
  assign out_17 = {out_14[4:2], debug_2[1]};
  assign out_20 = {AC_3, out_14[4:2], debug_2};
  assign out_21[1:0] = debug_3;
  assign out_22 = out_21[8:5];
  assign out_27 = {AC_4, out_21[4:2], debug_3};
  assign out_28[1:0] = debug_4;
  assign out_29 = out_28[8:5];
  assign out_31 = {out_28[4:2], debug_4[1]};
  assign out_34 = {AC_5, out_28[4:2], debug_4};
  assign out_36 = out_35[8:5];
  assign out_38 = out_35[4:1];
  assign out_39 = out_35[8:1];
  assign Q_1 = in_5;
  assign Q_2 = {out_21[4:2], debug_3[1]};
  assign Qn___1 = debug_2[0];
  assign Qn___1_2 = debug_3[0];
  assign Qn___1_3 = debug_4[0];
  assign Qn___1_4 = out_35[0];

  // Notes on the sheet:
  //   compliment
  //   non compliment
  //   1 bit right arithmetic shift 
  //   A
  //   compliment
  //   non compliment
  //   A
  //   compliment
  //   non compliment
  //   1 bit right arithmetic shift 
  //   A
  //   compliment
  //   non compliment
  //   1 bit right arithmetic shift 
  //   A
  //   1 bit right arithmetic shift 
  //   ANSWER
endmodule
