// Logisim project division non restoring.circ as structural Verilog: 1 circuit, main circuit main
module main (
  input  [4:0] A,
  input  [4:0] M_divisor,
  input  [3:0] Q_dvidend,
  input  [3:0] in_4,
  input  always_1,
  input  always_0,
  input  [3:0] in_7,
  input  always_1_2,
  input  always_0_2,
  input  [3:0] in_10,
  input  always_1_3,
  input  always_0_3,
  input  [3:0] in_13,
  input  always_1_4,
  input  always_0_4,
  output [8:0] out_16,
  output [8:0] out_17,
  output [3:0] out_18,
  output [4:0] out_19,
  output [4:0] out_20,
  output [4:0] out_21,
  output [3:0] Q_after_decision,
  output [8:0] out_23,
  output [8:0] out_24,
  output [3:0] out_25,
  output [4:0] out_26,
  output [4:0] out_27,
  output [4:0] out_28,
  output [3:0] out_29,
  output [8:0] out_30,
  output [8:0] out_31,
  output [3:0] out_32,
  output [4:0] out_33,
  output [4:0] out_34,
  output [4:0] out_35,
  output [3:0] Q_after_decision_2,
  output [8:0] out_37,
  output [8:0] out_38,
  output [3:0] out_39,
  output [4:0] out_40,
  output [4:0] out_41,
  output [4:0] out_42,
  output [3:0] Q_after_decision_3,
  output [3:0] out_44,
  output [4:0] out_45
);

  wire [4:0] adder_1_out, adder_2_out, adder_3_out, adder_4_out, adder_5_out, adder_6_out, adder_7_out,
       adder_8_out, adder_9_out, negator_1_out, negator_2_out, negator_3_out, negator_4_out;

  Adder #(.width(5)) adder_1 (.a(M_divisor), .b(out_17[8:4]), .out(adder_1_out));  // open: cin, cout
  Negator #(.width(5)) negator_1 (.in(M_divisor), .out(negator_1_out));
  Adder #(.width(5)) adder_2 (.a(out_17[8:4]), .b(negator_1_out), .out(adder_2_out));  // open: cin, cout
  Adder #(.width(5)) adder_3 (.a(M_divisor), .b(out_24[8:4]), .out(adder_3_out));  // open: cin, cout
  Negator #(.width(5)) negator_2 (.in(M_divisor), .out(negator_2_out));
  Adder #(.width(5)) adder_4 (.a(M_divisor), .b(out_31[8:4]), .out(adder_4_out));  // open: cin, cout
  Negator #(.width(5)) negator_3 (.in(M_divisor), .out(negator_3_out));
  Adder #(.width(5)) adder_5 (.a(M_divisor), .b(out_38[8:4]), .out(adder_5_out));  // open: cin, cout
  Negator #(.width(5)) negator_4 (.in(M_divisor), .out(negator_4_out));
  Adder #(.width(5)) adder_6 (.a(out_24[8:4]), .b(negator_2_out), .out(adder_6_out));  // open: cin, cout
  Shifter #(.width(9)) shifter_1 (.in({A, Q_dvidend}), .\dist (in_4), .out(out_17));
  Multiplexer #(.width(5)) multiplexer_1 (
    .in0(adder_2_out), .in1(adder_1_out), .out(out_21), .sel(out_17[8]));  // open: en
  Adder #(.width(5)) adder_7 (.a(out_31[8:4]), .b(negator_3_out), .out(adder_7_out));  // open: cin, cout
  Adder #(.width(5)) adder_8 (.a(out_38[8:4]), .b(negator_4_out), .out(adder_8_out));  // open: cin, cout
  Adder #(.width(5)) adder_9 (.a(out_42), .b(M_divisor), .out(adder_9_out));  // open: cin, cout
  Shifter #(.width(9)) shifter_2 (.in({out_21, out_23[3:0]}), .\dist (in_7), .out(out_24));
  Multiplexer #(.width(5)) multiplexer_2 (
    .in0(adder_6_out), .in1(adder_3_out), .out(out_28), .sel(out_24[8]));  // open: en
  Shifter #(.width(9)) shifter_3 (.in({out_28, out_29}), .\dist (in_10), .out(out_31));
  Multiplexer #(.width(5)) multiplexer_3 (
    .in0(adder_7_out), .in1(adder_4_out), .out(out_35), .sel(out_31[8]));  // open: en
  Shifter #(.width(9)) shifter_4 (.in({out_35, out_37[3:0]}), .\dist (in_13), .out(out_38));
  Multiplexer #(.width(5)) multiplexer_4 (
    .in0(adder_8_out), .in1(adder_5_out), .out(out_42), .sel(out_38[8]));  // open: en
  Multiplexer #(.width(5)) multiplexer_5 (.in0(out_42), .in1(adder_9_out), .out(out_45), .sel(out_42[4]));  // open: en
  Multiplexer #(.width(4)) multiplexer_6 (
    .in0({out_17[3:1], always_1}), .in1({out_17[3:1], always_0}), .out(out_23[3:0]), .sel(out_21[4]));  // open: en
  Multiplexer #(.width(4)) multiplexer_7 (
    .in0({out_24[3:1], always_1_2}), .in1({out_24[3:1], always_0_2}), .out(out_29), .sel(out_28[4]));  // open: en
  Multiplexer #(.width(4)) multiplexer_8 (
    .in0({out_38[3:1], always_1_4}), .in1({out_38[3:1], always_0_4}), .out(out_44), .sel(out_42[4]));  // open: en
  Multiplexer #(.width(4)) multiplexer_9 (
    .in0({out_31[3:1], always_1_3}), .in1({out_31[3:1], always_0_3}), .out(out_37[3:0]), .sel(out_35[4]));  // open: en

  assign out_16 = {A, Q_dvidend};
  assign out_18 = out_17[3:0];
  assign out_19 = out_17[8:4];
  assign out_23[8:4] = out_21;
  assign out_25 = out_24[3:0];
  assign out_26 = out_24[8:4];
  assign out_30 = {out_28, out_29};
  assign out_32 = out_31[3:0];
  assign out_33 = out_31[8:4];
  assign out_37[8:4] = out_35;
  assign out_39 = out_38[3:0];
  assign out_40 = out_38[8:4];
  assign Q_after_decision = out_23[3:0];
  assign Q_after_decision_2 = out_37[3:0];
  assign Q_after_decision_3 = out_44;

  // Notes on the sheet:
  //   A 
  //   M
  //   A+M
  //   A 
  //   M
  //   M
  //   A 
  //   M
  //   REMAINDER
  //   A
  //   A - M
  //   A+M
  //   A 
  //   A+M
  //   A+M
  //   Q
  //   1 bit left shift 
  //   A after decision 
  //   A
  //   A - M
  //   A
  //   A - M
  //   A
  //   A - M
  //   sign bit of A 
  //   decision bit
  //   Q
  //   1 bit left shift 
  //   A after decision 
  //   Q
  //   1 bit left shift 
  //   A after decision 
  //   Q
  //   1 bit left shift 
  //   A after decision 
  //   AQ combined
  //   A
  //   sign bit of A 
  //   decision bit
  //   sign bit of A 
  //   decision bit
  //   sign bit of A 
  //   decision bit
  //   sign bit of A 
  //   decision bit
  //   Q
  //   AQ combined
  //   A
  //   sign bit of A 
  //   decision bit
  //   A
  //   sign bit of A 
  //   decision bit
  //   A
  //   sign bit of A 
  //   decision bit
  //   Q for A[sign 0]
  //   Q
  //   AQ combined
  //   Q
  //   AQ combined
  //   Q
  //   QOUTIENT
  //   Q for A[sign 0]
  //   Q for A[sign 0]
  //   Q for A[sign 0]
  //   set 1 and zeroes in q calc and shiftervalue
endmodule
