// Logisim project division restoring.circ as structural Verilog: 1 circuit, main circuit main
module main (
  input  [3:0] A,
  input  [3:0] divisor,
  input  [3:0] dividend_Q,
  input  [2:0] in_4,
  input  always_0,
  input  in_6,
  input  [2:0] in_7,
  input  always_0_2,
  input  in_9,
  input  [2:0] in_10,
  input  always_0_3,
  input  in_12,
  input  [2:0] in_13,
  input  always_0_4,
  input  in_15,
  output [7:0] before_shift,
  output [7:0] out_17,
  output [3:0] out_18,
  output [3:0] out_19,
  output [3:0] out_20,
  output [3:0] out_21,
  output [7:0] before_shift_2,
  output [7:0] out_23,
  output [3:0] A_2,
  output [3:0] out_25,
  output [3:0] out_26,
  output [3:0] out_27,
  output [3:0] out_28,
  output [7:0] before_shift_3,
  output [7:0] out_30,
  output [3:0] out_31,
  output [3:0] out_32,
  output [3:0] out_33,
  output [3:0] out_34,
  output [7:0] before_shift_4,
  output [7:0] out_36,
  output [3:0] out_37,
  output [3:0] out_38,
  output [3:0] out_39,
  output [3:0] out_40,
  output [3:0] out_41,
  output [3:0] REMINDER
);

  wire [3:0] negator_1_out, negator_2_out, negator_3_out, negator_4_out;

  Negator #(.width(4)) negator_1 (.in(divisor), .out(negator_1_out));
  Negator #(.width(4)) negator_2 (.in(divisor), .out(negator_2_out));
  Shifter shifter_1 (.in({A, dividend_Q}), .\dist (in_4), .out(out_17));
  Adder #(.width(4)) adder_1 (.a(out_17[7:4]), .b(negator_1_out), .out(out_19));  // open: cin, cout
  Shifter shifter_2 (.in(before_shift_2), .\dist (in_7), .out({A_2, out_23[3:0]}));
  Adder #(.width(4)) adder_2 (.a(A_2), .b(negator_2_out), .out(out_26));  // open: cin, cout
  Shifter shifter_3 (.in(before_shift_3), .\dist (in_10), .out(out_30));
  Negator #(.width(4)) negator_3 (.in(divisor), .out(negator_3_out));
  Shifter shifter_4 (.in(before_shift_4), .\dist (in_13), .out(out_36));
  Negator #(.width(4)) negator_4 (.in(divisor), .out(negator_4_out));
  Adder #(.width(4)) adder_3 (.a(out_30[7:4]), .b(negator_3_out), .out(out_32));  // open: cin, cout
  Adder #(.width(4)) adder_4 (.a(out_36[7:4]), .b(negator_4_out), .out(out_38));  // open: cin, cout
  Multiplexer #(.width(4)) multiplexer_1 (
    .in0(out_19), .in1(out_17[7:4]), .out(before_shift_2[7:4]), .sel(out_19[3]));  // open: en
  Multiplexer #(.width(4)) multiplexer_2 (
    .in0({out_17[3:1], in_6}), .in1({out_17[3:1], always_0}), .out(before_shift_2[3:0]), .sel(out_19[3]));  // open: en
  Multiplexer #(.width(4)) multiplexer_3 (
    .in0(out_26), .in1(A_2), .out(before_shift_3[7:4]), .sel(out_26[3]));  // open: en
  Multiplexer #(.width(4)) multiplexer_4 (
    .in0({out_23[3:1], in_9}), .in1({out_23[3:1], always_0_2}), .out(before_shift_3[3:0]), .sel(out_26[3]));  // open: en
  Multiplexer #(.width(4)) multiplexer_5 (
    .in0(out_32), .in1(out_30[7:4]), .out(before_shift_4[7:4]), .sel(out_32[3]));  // open: en
  Multiplexer #(.width(4)) multiplexer_6 (
    .in0({out_30[3:1], in_12}), .in1({out_30[3:1], always_0_3}), .out(before_shift_4[3:0]), .sel(out_32[3]));  // open: en
  Multiplexer #(.width(4)) multiplexer_7 (.in0(out_38), .in1(out_36[7:4]), .out(out_40), .sel(out_38[3]));  // open: en
  Multiplexer #(.width(4)) multiplexer_8 (
    .in0({out_36[3:1], in_15}), .in1({out_36[3:1], always_0_4}), .out(out_39), .sel(out_38[3]));  // open: en

  assign before_shift = {A, dividend_Q};
  assign out_18 = out_17[3:0];
  assign out_20 = before_shift_2[3:0];
  assign out_21 = before_shift_2[7:4];
  assign out_23[7:4] = A_2;
  assign out_25 = out_23[3:0];
  assign out_27 = before_shift_3[3:0];
  assign out_28 = before_shift_3[7:4];
  assign out_31 = out_30[3:0];
  assign out_33 = before_shift_4[3:0];
  assign out_34 = before_shift_4[7:4];
  assign out_37 = out_36[3:0];
  assign out_41 = out_39;
  assign REMINDER = out_40;

  // Notes on the sheet:
  //   A
  //   Q
  //   divisor
  //   A
  //   Q
  //   divisor
  //   Q
  //   divisor
  //   divisor
  //   1 bit left shift
  //   1 bit left shift
  //   A
  //   A
  //   Q
  //   1 bit left shift
  //   1 bit left shift
  //   QOUTIENT
  //   after shift
  //   A
  //   after shift
  //   A
  //   A
  //   Q
  //   Q
  //   after shift
  //   Q
  //   after shift
  //   most sig bit of A
  //   most sig bit of A
  //   Q
  //   most sig bit of A
  //   most sig bit of A
  //   for A
  //   for Q
  //   for A
  //   for Q
  //   always 1
  //   Q
  //   always 1
  //   Q
  //   for A
  //   for Q
  //   for A
  //   for Q
  //   A
  //   A
  //   always 1
  //   Q
  //   always 1
  //   Q
  //   A
  //   A
endmodule
